// Logisim project control_logic.circ as structural Verilog: 1 circuit, main circuit control_logic
module control_logic (
  input  [31:0] inst,
  input  BrEq,
  input  BrLt,
  output PCSel,
  output RegWEn,
  output [2:0] ImmSel,
  output BrUn,
  output ASel,
  output BSel,
  output [3:0] ALUSel,
  output MemRW,
  output [1:0] WBSel,
  output CSRSel,
  output CSRWen,
  output isLb,
  output isLh,
  output isSb,
  output isSh
);

  wire and_7_out, and_8_out, and_9_out, and_10_out, and_11_out, and_12_out, comparator_1_eq, comparator_2_eq,
       comparator_3_eq, comparator_4_eq, comparator_5_eq, comparator_6_eq, comparator_9_eq, comparator_10_eq,
       comparator_12_eq, comparator_13_eq, comparator_14_eq, comparator_15_eq, comparator_16_eq,
       comparator_17_eq, comparator_18_eq, comparator_19_eq, comparator_20_eq, comparator_22_eq,
       comparator_23_eq, comparator_24_eq, comparator_25_eq, comparator_26_eq, comparator_27_eq,
       comparator_28_eq, comparator_29_eq, comparator_30_eq, comparator_31_eq, comparator_32_eq,
       comparator_33_eq, comparator_34_eq, comparator_35_eq, comparator_36_eq, comparator_37_eq,
       comparator_38_eq, comparator_39_eq, comparator_40_eq, comparator_41_eq, comparator_42_eq,
       comparator_43_eq, comparator_45_eq, comparator_46_eq, comparator_47_eq, comparator_48_eq,
       comparator_49_eq, comparator_50_eq, comparator_51_eq, comparator_52_eq, comparator_53_eq,
       comparator_54_eq, comparator_55_eq, comparator_56_eq, InstB, InstU, InstUJ, isIorR, isMul, isMulh,
       isSra, isSub, not_1_out, not_2_out, not_3_out, or_2_out, or_9_out, or_10_out, WBSelALU, WBSelImm,
       WBSelPC4;
  wire [1:0] multiplexer_12_out, multiplexer_13_out;
  wire [2:0] multiplexer_2_out, multiplexer_3_out, multiplexer_5_out, multiplexer_8_out;
  wire [3:0] multiplexer_1_out, multiplexer_4_out, multiplexer_6_out, multiplexer_7_out, multiplexer_10_out;

  Multiplexer #(.enable("false"), .select(3), .width(4)) multiplexer_1 (
    .in0(4'b0000), .in1(4'b0110), .in2(4'b0111), .in3(4'b1011), .in4(4'b0011), .in5(4'b0100), .in6(4'b0010),
    .in7(4'b0001), .out(multiplexer_1_out), .sel(inst[14:12]));
  Multiplexer #(.enable("false"), .width(3)) multiplexer_2 (
    .in0(3'b000), .in1(3'b001), .out(multiplexer_2_out), .sel(MemRW));
  Comparator #(.width(7)) comparator_1 (.a(inst[31:25]), .b(7'b0000001), .eq(comparator_1_eq));  // open: gt, lt
  Comparator #(.width(3)) comparator_2 (.a(inst[14:12]), .b(3'b000), .eq(comparator_2_eq));  // open: gt, lt
  Comparator #(.width(7)) comparator_3 (.a(inst[6:0]), .b(7'b0110011), .eq(comparator_3_eq));  // open: gt, lt
  Comparator #(.width(7)) comparator_4 (.a(inst[31:25]), .b(7'b0000001), .eq(comparator_4_eq));  // open: gt, lt
  Comparator #(.width(3)) comparator_5 (.a(inst[14:12]), .b(3'b001), .eq(comparator_5_eq));  // open: gt, lt
  Comparator #(.width(7)) comparator_6 (.a(inst[6:0]), .b(7'b0110011), .eq(comparator_6_eq));  // open: gt, lt
  Multiplexer #(.enable("false"), .width(3)) multiplexer_3 (
    .in0(multiplexer_2_out), .in1(3'b010), .out(multiplexer_3_out), .sel(InstB));
  Multiplexer #(.enable("false"), .width(4)) multiplexer_4 (
    .in0(multiplexer_1_out), .in1(4'b1010), .out(multiplexer_4_out), .sel(isMul));
  and and_1 (isMul, comparator_1_eq, comparator_2_eq, comparator_3_eq);
  and and_2 (isMulh, comparator_4_eq, comparator_5_eq, comparator_6_eq);
  Comparator #(.width(7)) comparator_7 (.a(inst[6:0]), .b(7'b0100011), .eq(MemRW));  // open: gt, lt
  Comparator #(.width(7)) comparator_8 (.a(inst[6:0]), .b(7'b1100011), .eq(InstB));  // open: gt, lt
  Comparator #(.width(7)) comparator_9 (.a(inst[6:0]), .b(7'b0010111), .eq(comparator_9_eq));  // open: gt, lt
  Comparator #(.width(7)) comparator_10 (.a(inst[6:0]), .b(7'b0110111), .eq(comparator_10_eq));  // open: gt, lt
  Comparator #(.width(7)) comparator_11 (.a(inst[6:0]), .b(7'b1101111), .eq(InstUJ));  // open: gt, lt
  Comparator #(.width(7)) comparator_12 (.a(inst[6:0]), .b(7'b1110011), .eq(comparator_12_eq));  // open: gt, lt
  Comparator #(.width(3)) comparator_13 (.a(inst[14:12]), .b(3'b101), .eq(comparator_13_eq));  // open: gt, lt
  Multiplexer #(.enable("false"), .width(3)) multiplexer_5 (
    .in0(multiplexer_3_out), .in1(3'b011), .out(multiplexer_5_out), .sel(InstU));
  Comparator #(.width(7)) comparator_14 (.a(inst[6:0]), .b(7'b1110011), .eq(comparator_14_eq));  // open: gt, lt
  Comparator #(.width(3)) comparator_15 (.a(inst[14:12]), .b(3'b101), .eq(comparator_15_eq));  // open: gt, lt
  Multiplexer #(.enable("false"), .width(4)) multiplexer_6 (
    .in0(multiplexer_4_out), .in1(4'b1011), .out(multiplexer_6_out), .sel(isMulh));
  or or_1 (InstU, comparator_9_eq, comparator_10_eq);
  and and_3 (CSRSel, comparator_12_eq, comparator_13_eq);
  or or_2 (or_2_out, comparator_14_eq, comparator_15_eq);
  Multiplexer #(.enable("false"), .width(4)) multiplexer_7 (
    .in0(multiplexer_6_out), .in1(4'b1100), .out(multiplexer_7_out), .sel(isSub));
  Multiplexer #(.enable("false"), .width(3)) multiplexer_8 (
    .in0(multiplexer_5_out), .in1(3'b100), .out(multiplexer_8_out), .sel(InstUJ));
  Multiplexer #(.enable("false"), .width(3)) multiplexer_9 (
    .in0(multiplexer_8_out), .in1(3'b101), .out(ImmSel), .sel(CSRSel));
  and and_4 (BrUn, InstB, or_2_out);
  Multiplexer #(.enable("false"), .width(4)) multiplexer_10 (
    .in0(multiplexer_7_out), .in1(4'b1100), .out(multiplexer_10_out), .sel(isSra));
  Comparator #(.width(7)) comparator_16 (.a(inst[31:25]), .b(7'b0100000), .eq(comparator_16_eq));  // open: gt, lt
  Comparator #(.width(3)) comparator_17 (.a(inst[14:12]), .b(3'b000), .eq(comparator_17_eq));  // open: gt, lt
  Comparator #(.width(7)) comparator_18 (.a(inst[6:0]), .b(7'b0110011), .eq(comparator_18_eq));  // open: gt, lt
  Comparator #(.width(7)) comparator_19 (.a(inst[31:25]), .b(7'b0100000), .eq(comparator_19_eq));  // open: gt, lt
  Comparator #(.width(3)) comparator_20 (.a(inst[14:12]), .b(3'b101), .eq(comparator_20_eq));  // open: gt, lt
  Multiplexer #(.enable("false"), .width(4)) multiplexer_11 (
    .in0(4'b0000), .in1(multiplexer_10_out), .out(ALUSel), .sel(isIorR));
  Comparator #(.width(7)) comparator_21 (.a(inst[6:0]), .b(7'b1110011), .eq(CSRWen));  // open: gt, lt
  and and_5 (isSub, comparator_16_eq, comparator_17_eq, comparator_18_eq);
  and and_6 (isSra, comparator_19_eq, comparator_20_eq);
  Comparator #(.width(7)) comparator_22 (.a(inst[6:0]), .b(7'b0110011), .eq(comparator_22_eq));  // open: gt, lt
  Comparator #(.width(7)) comparator_23 (.a(inst[6:0]), .b(7'b0010011), .eq(comparator_23_eq));  // open: gt, lt
  Comparator #(.width(7)) comparator_24 (.a(inst[6:0]), .b(7'b0110011), .eq(comparator_24_eq));  // open: gt, lt
  Comparator #(.width(7)) comparator_25 (.a(inst[6:0]), .b(7'b0000011), .eq(comparator_25_eq));  // open: gt, lt
  Comparator #(.width(7)) comparator_26 (.a(inst[6:0]), .b(7'b0010011), .eq(comparator_26_eq));  // open: gt, lt
  Comparator #(.width(7)) comparator_27 (.a(inst[6:0]), .b(7'b1101111), .eq(comparator_27_eq));  // open: gt, lt
  Comparator #(.width(7)) comparator_28 (.a(inst[6:0]), .b(7'b0110111), .eq(comparator_28_eq));  // open: gt, lt
  Comparator #(.width(7)) comparator_29 (.a(inst[6:0]), .b(7'b0010111), .eq(comparator_29_eq));  // open: gt, lt
  Comparator #(.width(7)) comparator_30 (.a(inst[6:0]), .b(7'b1100111), .eq(comparator_30_eq));  // open: gt, lt
  Comparator #(.width(7)) comparator_31 (.a(inst[6:0]), .b(7'b0010111), .eq(comparator_31_eq));  // open: gt, lt
  or or_3 (isIorR, comparator_22_eq, comparator_23_eq);
  or or_4 (RegWEn, comparator_24_eq, comparator_25_eq, comparator_26_eq, comparator_27_eq, comparator_28_eq, comparator_29_eq, comparator_30_eq);
  or or_5 (ASel, InstB, InstUJ, comparator_31_eq);
  Multiplexer #(.enable("false"), .width(2)) multiplexer_12 (
    .in0(2'b00), .in1(2'b01), .out(multiplexer_12_out), .sel(WBSelALU));
  Comparator #(.width(7)) comparator_32 (.a(inst[6:0]), .b(7'b0010011), .eq(comparator_32_eq));  // open: gt, lt
  Comparator #(.width(7)) comparator_33 (.a(inst[6:0]), .b(7'b0000011), .eq(comparator_33_eq));  // open: gt, lt
  Comparator #(.width(7)) comparator_34 (.a(inst[6:0]), .b(7'b1100011), .eq(comparator_34_eq));  // open: gt, lt
  Comparator #(.width(7)) comparator_35 (.a(inst[6:0]), .b(7'b1100111), .eq(comparator_35_eq));  // open: gt, lt
  Comparator #(.width(7)) comparator_36 (.a(inst[6:0]), .b(7'b0010111), .eq(comparator_36_eq));  // open: gt, lt
  Comparator #(.width(7)) comparator_37 (.a(inst[6:0]), .b(7'b0110111), .eq(comparator_37_eq));  // open: gt, lt
  Comparator #(.width(7)) comparator_38 (.a(inst[6:0]), .b(7'b1101111), .eq(comparator_38_eq));  // open: gt, lt
  Comparator #(.width(7)) comparator_39 (.a(inst[6:0]), .b(7'b0010011), .eq(comparator_39_eq));  // open: gt, lt
  Comparator #(.width(7)) comparator_40 (.a(inst[6:0]), .b(7'b0010111), .eq(comparator_40_eq));  // open: gt, lt
  Comparator #(.width(7)) comparator_41 (.a(inst[6:0]), .b(7'b0110011), .eq(comparator_41_eq));  // open: gt, lt
  Comparator #(.width(7)) comparator_42 (.a(inst[6:0]), .b(7'b1100111), .eq(comparator_42_eq));  // open: gt, lt
  Comparator #(.width(7)) comparator_43 (.a(inst[6:0]), .b(7'b1101111), .eq(comparator_43_eq));  // open: gt, lt
  Comparator #(.width(7)) comparator_44 (.a(inst[6:0]), .b(7'b0110111), .eq(WBSelImm));  // open: gt, lt
  Multiplexer #(.enable("false"), .width(2)) multiplexer_13 (
    .in0(multiplexer_12_out), .in1(2'b10), .out(multiplexer_13_out), .sel(WBSelPC4));
  or or_6 (BSel, comparator_32_eq, comparator_33_eq, comparator_34_eq, comparator_35_eq, comparator_36_eq, comparator_37_eq, comparator_38_eq);
  or or_7 (WBSelALU, comparator_39_eq, comparator_40_eq, comparator_41_eq);
  or or_8 (WBSelPC4, comparator_42_eq, comparator_43_eq);
  Multiplexer #(.enable("false"), .width(2)) multiplexer_14 (
    .in0(multiplexer_13_out), .in1(2'b11), .out(WBSel), .sel(WBSelImm));
  Comparator #(.width(3)) comparator_45 (.a(inst[14:12]), .b(3'b000), .eq(comparator_45_eq));  // open: gt, lt
  Comparator #(.width(3)) comparator_46 (.a(inst[14:12]), .b(3'b001), .eq(comparator_46_eq));  // open: gt, lt
  Comparator #(.width(3)) comparator_47 (.a(inst[14:12]), .b(3'b100), .eq(comparator_47_eq));  // open: gt, lt
  Comparator #(.width(3)) comparator_48 (.a(inst[14:12]), .b(3'b101), .eq(comparator_48_eq));  // open: gt, lt
  Comparator #(.width(3)) comparator_49 (.a(inst[14:12]), .b(3'b110), .eq(comparator_49_eq));  // open: gt, lt
  Comparator #(.width(3)) comparator_50 (.a(inst[14:12]), .b(3'b111), .eq(comparator_50_eq));  // open: gt, lt
  Comparator #(.width(7)) comparator_51 (.a(inst[6:0]), .b(7'b0000011), .eq(comparator_51_eq));  // open: gt, lt
  Comparator #(.width(7)) comparator_52 (.a(inst[6:0]), .b(7'b0100011), .eq(comparator_52_eq));  // open: gt, lt
  Comparator #(.width(3)) comparator_53 (.a(inst[14:12]), .b(3'b000), .eq(comparator_53_eq));  // open: gt, lt
  Comparator #(.width(3)) comparator_54 (.a(inst[14:12]), .b(3'b001), .eq(comparator_54_eq));  // open: gt, lt
  not not_1 (not_1_out, BrEq);
  not not_2 (not_2_out, BrLt);
  not not_3 (not_3_out, BrLt);
  and and_7 (and_7_out, InstB, comparator_45_eq, BrEq);
  and and_8 (and_8_out, InstB, comparator_46_eq, not_1_out);
  and and_9 (and_9_out, InstB, comparator_47_eq, BrLt);
  and and_10 (and_10_out, InstB, comparator_48_eq, not_2_out);
  and and_11 (and_11_out, InstB, comparator_49_eq, BrLt);
  and and_12 (and_12_out, InstB, comparator_50_eq, not_3_out);
  and and_13 (isLb, comparator_51_eq, comparator_53_eq);
  and and_14 (isLh, comparator_51_eq, comparator_54_eq);
  and and_15 (isSb, comparator_52_eq, comparator_53_eq);
  and and_16 (isSh, comparator_52_eq, comparator_54_eq);
  Comparator #(.width(7)) comparator_55 (.a(inst[6:0]), .b(7'b1100111), .eq(comparator_55_eq));  // open: gt, lt
  Comparator #(.width(7)) comparator_56 (.a(inst[6:0]), .b(7'b1101111), .eq(comparator_56_eq));  // open: gt, lt
  or or_9 (or_9_out, and_7_out, and_8_out, and_9_out, and_10_out, and_11_out, and_12_out);
  or or_10 (or_10_out, comparator_55_eq, comparator_56_eq);
  or or_11 (PCSel, or_9_out, or_10_out);

  // Other names for the same wires on the sheet: op[6:0] = inst[6:0]; rd[4:0] = inst[11:7]; funct3[2:0] = inst[14:12];
  //   rs1[4:0] = inst[19:15]; rs2[4:0] = inst[24:20]; funct7[6:0] = inst[31:25]; InstCSR = CSRSel; InstS = MemRW

  // Notes on the sheet:
  //   INPUTS to your circuit
  //   decode
  //   Imm select: I, S, B, U, J, CSR
  //   ALU select
  //   DON'T CHANGE THE LOCATIONS OF THE INPUTS AND OUTPUTS!
  //   OUTPUT from your circuit
  //   Register Write Enable
  //   ASel: select from PC and rs1
  //   BSel: select from rs2 and imm
  //   WBSel: select from memory, ALU, PC+4, Imm
  //   PCSel: select from PC+4 and ALU
  //   Write mask
endmodule
