// Logisim project cpu.circ as structural Verilog: 1 circuit, main circuit cpu
module cpu (
  input  clk,
  input  [31:0] INSTRUCTION,
  input  [31:0] READ_DATA,
  output [31:0] WRITE_ADDRESS,
  output [31:0] PROGRAM_COUNTER,
  output [31:0] ra,
  output [31:0] sp,
  output [31:0] t0,
  output [31:0] t1,
  output [31:0] t2,
  output [31:0] s0,
  output [31:0] s1,
  output [31:0] a0,
  output [31:0] tohost,
  output [3:0] WRITE_ENABLE,
  output [31:0] WRITE_DATA
);

  wire RegWEn;
  wire [2:0] funct3;
  wire [3:0] ALUSel;
  wire [6:0] funct7;
  wire [24:0] INSTRUCTION_t;
  wire [31:0] adder_1_out, ALU_OUT, data1, imm, PROGRAM_COUNTER_t, WB_DATA;

  Adder #(.width(32)) adder_1 (.a(PROGRAM_COUNTER), .b(32'h4), .out(adder_1_out));  // open: cin, cout
  Register #(.width(32)) PC (.D(adder_1_out), .clk(clk), .Q(PROGRAM_COUNTER));  // open: en, clr
  Register #(.width(32)) register_1 (.D(PROGRAM_COUNTER), .clk(clk), .Q(PROGRAM_COUNTER_t));  // open: en, clr
  Register #(.width(32)) register_2 (
    .D(INSTRUCTION), .clk(clk), .Q({funct7, INSTRUCTION_t[24:15], funct3, INSTRUCTION_t[11:0]}));  // open: en, clr
  imm_gen imm_gen_1 (.inst({funct7, INSTRUCTION_t[24:15], funct3, INSTRUCTION_t[11:0]}), .imm(imm));  // open: ImmSel
  control_logic control_logic_1 (
    .RegWEn(RegWEn), .ALUSel(ALUSel), .inst({funct7, INSTRUCTION_t[24:15], funct3, INSTRUCTION_t[11:0]}));  // open: CSRWen, PCSel, ImmSel, BrUn, ASel, BSel, MemRW, WBSel, CSRSel, BrEq, BrLt
  regfile regfile_1 (
    .rs1(INSTRUCTION_t[19:15]), .rs2(INSTRUCTION_t[24:20]), .rd(INSTRUCTION_t[11:7]), .Write_Data(WB_DATA),
    .RegWEn(RegWEn), .clk(clk), .ra(ra), .sp(sp), .t0(t0), .t1(t1), .t2(t2), .s0(s0), .s1(s1), .a0(a0),
    .Read_Data_1(data1));  // open: Read_Data_2
  // branch_comp branch_comp_1: pin names not known
  alu alu_1 (.Result(ALU_OUT), .A(data1), .B(imm), .ALUSel(ALUSel));
  csr csr_1 (.tohost(tohost));  // open: CSR_address, CSR_din, CSR_WE, clk
  Multiplexer #(.enable("false"), .width(32)) multiplexer_1 (.in0(ALU_OUT), .in1(READ_DATA), .out(WB_DATA), .sel(1'b0));

  // Other names for the same wires on the sheet: IN_temporary[31:0] = INSTRUCTION; op[6:0] = INSTRUCTION_t[6:0];
  //   rd[4:0] = INSTRUCTION_t[11:7]; INSTRUCTION_t (some bits) = {funct7, funct3}; rs1[4:0] = INSTRUCTION_t[19:15];
  //   rs2[4:0] = INSTRUCTION_t[24:20]; PC_temporary[31:0] = PROGRAM_COUNTER

  // Notes on the sheet:
  //   Output to IMEM
  //   IMEM (do **NOT** move this)
  //   Inputs from IMEM
  //   It is OK to move the PC, RegFile, ALU, MEM, Branch Comp, Imm Gen, and Control Logic to wherever is most convenient for you when constructing your CPU, and to delete this text
  //   Inputs/Outputs for testing. Do **NOT** move these.
  //   Outputs To DMEM
  //   DMEM (do **NOT** move this)
  //   Inputs From DMEM
endmodule
